// Digital circuit Multiplicador .dig as structural Verilog
module Multiplicador (
  input  B4,
  input  B3,
  input  B2,
  input  B1,
  input  B0,
  input  A4,
  input  A3,
  input  A2,
  input  A1,
  input  A0,
  output \Saída0 ,
  output \Saída1 ,
  output \Saída2 ,
  output \Saída3 ,
  output \Saída4 ,
  output \Saída5 ,
  output \Saída6 ,
  output \Saída7 ,
  output \Saída8 ,
  output \Saída9 
);

  wire B0_A1_p3, B0_A2_p3, B0_A3_p3, B0_A4_p3, B1_A0_p3, B1_A1_p3, B1_A2_p3, B1_A3_p3, B1_A4_p3, B2_A0_p3,
       B2_A1_p3, B2_A2_p3, B2_A3_p3, B2_A4_p3, B3_A0_p3, B3_A1_p3, B3_A2_p3, B3_A3_p3, B3_A4_p3, B4_A0_p3,
       B4_A1_p3, B4_A2_p3, B4_A3_p3, B4_A4_p6, full_adder_com_xor_1_p3, full_adder_com_xor_1_p4,
       full_adder_com_xor_1_p5, full_adder_com_xor_2_p4, full_adder_com_xor_2_p5, full_adder_com_xor_3_p4,
       full_adder_com_xor_3_p5, full_adder_com_xor_4_p4, full_adder_com_xor_4_p5, full_adder_com_xor_5_p4,
       full_adder_com_xor_5_p5, full_adder_com_xor_6_p4, full_adder_com_xor_7_p3, full_adder_com_xor_8_p3,
       full_adder_com_xor_8_p4, full_adder_com_xor_8_p5, full_adder_com_xor_9_p3, full_adder_com_xor_9_p4,
       full_adder_com_xor_9_p5, full_adder_com_xor_10_p4, full_adder_com_xor_10_p5, full_adder_com_xor_11_p4,
       full_adder_com_xor_12_p3, full_adder_com_xor_13_p4, full_adder_com_xor_13_p5,
       full_adder_com_xor_14_p2, full_adder_com_xor_14_p3, full_adder_com_xor_15_p4, halfadder_1_p3,
       halfadder_3_p3, halfadder_4_p3;

  // porta_AND B0_A0: pin names not known; wires that end beside it: B0, A0, \Saída0 
  // porta_AND B0_A1: pin names not known; wires that end beside it: B0, A1, B0_A1_p3
  // porta_AND B1_A0: pin names not known; wires that end beside it: B1, A0, B1_A0_p3
  // porta_AND B0_A2: pin names not known; wires that end beside it: B0, A2, B0_A2_p3
  // porta_AND B1_A1: pin names not known; wires that end beside it: B1, A1, B1_A1_p3
  // porta_AND B2_A0: pin names not known; wires that end beside it: B2, A0, B2_A0_p3
  // porta_AND B0_A3: pin names not known; wires that end beside it: B0, A3, B0_A3_p3
  // porta_AND B1_A2: pin names not known; wires that end beside it: B1, A2, B1_A2_p3
  // porta_AND B2_A1: pin names not known; wires that end beside it: B2, A1, B2_A1_p3
  // porta_AND B3_A0: pin names not known; wires that end beside it: B3, A0, B3_A0_p3
  // porta_AND B0_A4: pin names not known; wires that end beside it: B0, A4, B0_A4_p3
  // porta_AND B1_A3: pin names not known; wires that end beside it: B1, A3, B1_A3_p3
  // porta_AND B2_A2: pin names not known; wires that end beside it: B2, A2, B2_A2_p3
  // porta_AND B3_A1: pin names not known; wires that end beside it: B3, A1, B3_A1_p3
  // porta_AND B4_A0: pin names not known; wires that end beside it: B4, A0, B4_A0_p3
  // porta_AND B1_A4: pin names not known; wires that end beside it: B1, A4, B1_A4_p3
  // porta_AND B2_A3: pin names not known; wires that end beside it: B2, A3, B2_A3_p3
  // porta_AND B3_A2: pin names not known; wires that end beside it: B3, A2, B3_A2_p3
  // porta_AND B4_A1: pin names not known; wires that end beside it: B4, A1, B4_A1_p3
  // porta_AND B2_A4: pin names not known; wires that end beside it: B2, A4, B2_A4_p3
  // porta_AND B3_A3: pin names not known; wires that end beside it: B3, A3, B3_A3_p3
  // porta_AND B4_A2: pin names not known; wires that end beside it: B4, A2, B4_A2_p3
  // porta_AND B3_A4: pin names not known; wires that end beside it: B3, A4, B3_A4_p3
  // porta_AND B4_A3: pin names not known; wires that end beside it: B4, A3, B4_A3_p3
  // porta_AND B4_A4: pin names not known; wires that end beside it: A2, A1, A0, B4, A4, B4_A4_p6
  // halfadder halfadder_1: pin names not known; wires that end beside it: B0_A1_p3, B1_A0_p3, halfadder_1_p3, \Saída1 
  // full_adder_com_xor full_adder_com_xor_1: pin names not known; wires that end beside it: B0_A3_p3, B1_A2_p3, full_adder_com_xor_1_p3, full_adder_com_xor_1_p4, full_adder_com_xor_1_p5
  // full_adder_com_xor full_adder_com_xor_2: pin names not known; wires that end beside it: B0_A4_p3, B1_A3_p3, full_adder_com_xor_1_p5, full_adder_com_xor_2_p4, full_adder_com_xor_2_p5
  // full_adder_com_xor full_adder_com_xor_3: pin names not known; wires that end beside it: B1_A4_p3, B2_A3_p3, full_adder_com_xor_2_p5, full_adder_com_xor_3_p4, full_adder_com_xor_3_p5
  // full_adder_com_xor full_adder_com_xor_4: pin names not known; wires that end beside it: B2_A4_p3, B3_A3_p3, full_adder_com_xor_3_p5, full_adder_com_xor_4_p4, full_adder_com_xor_4_p5
  // full_adder_com_xor full_adder_com_xor_5: pin names not known; wires that end beside it: B3_A4_p3, B4_A3_p3, full_adder_com_xor_4_p5, full_adder_com_xor_5_p4, full_adder_com_xor_5_p5
  // full_adder_com_xor full_adder_com_xor_6: pin names not known; wires that end beside it: B0_A2_p3, B1_A1_p3, halfadder_1_p3, full_adder_com_xor_6_p4, full_adder_com_xor_1_p3
  // full_adder_com_xor full_adder_com_xor_7: pin names not known; wires that end beside it: B4_A4_p6, full_adder_com_xor_5_p5, full_adder_com_xor_7_p3, \Saída8 , \Saída9 
  // full_adder_com_xor full_adder_com_xor_8: pin names not known; wires that end beside it: B2_A1_p3, B3_A0_p3, full_adder_com_xor_8_p3, full_adder_com_xor_8_p4, full_adder_com_xor_8_p5
  // full_adder_com_xor full_adder_com_xor_9: pin names not known; wires that end beside it: full_adder_com_xor_4_p4, B4_A2_p3, full_adder_com_xor_9_p3, full_adder_com_xor_9_p4, full_adder_com_xor_9_p5
  // halfadder halfadder_2: pin names not known; wires that end beside it: full_adder_com_xor_6_p4, B2_A0_p3, full_adder_com_xor_8_p3, \Saída2 
  // full_adder_com_xor full_adder_com_xor_10: pin names not known; wires that end beside it: B2_A2_p3, B3_A1_p3, full_adder_com_xor_8_p5, full_adder_com_xor_10_p4, full_adder_com_xor_10_p5
  // full_adder_com_xor full_adder_com_xor_11: pin names not known; wires that end beside it: B3_A2_p3, B4_A1_p3, full_adder_com_xor_10_p5, full_adder_com_xor_11_p4, full_adder_com_xor_9_p3
  // halfadder halfadder_3: pin names not known; wires that end beside it: full_adder_com_xor_1_p4, full_adder_com_xor_8_p4, halfadder_3_p3, \Saída3 
  // full_adder_com_xor full_adder_com_xor_12: pin names not known; wires that end beside it: full_adder_com_xor_5_p4, full_adder_com_xor_9_p5, full_adder_com_xor_12_p3, \Saída7 , full_adder_com_xor_7_p3, \Saída7 
  // full_adder_com_xor full_adder_com_xor_13: pin names not known; wires that end beside it: full_adder_com_xor_10_p4, B4_A0_p3, halfadder_3_p3, full_adder_com_xor_13_p4, full_adder_com_xor_13_p5
  // full_adder_com_xor full_adder_com_xor_14: pin names not known; wires that end beside it: full_adder_com_xor_9_p4, full_adder_com_xor_14_p2, full_adder_com_xor_14_p3, \Saída6 , full_adder_com_xor_12_p3
  // halfadder halfadder_4: pin names not known; wires that end beside it: full_adder_com_xor_2_p4, full_adder_com_xor_13_p4, halfadder_4_p3, \Saída4 
  // full_adder_com_xor full_adder_com_xor_15: pin names not known; wires that end beside it: full_adder_com_xor_3_p4, full_adder_com_xor_11_p4, full_adder_com_xor_13_p5, full_adder_com_xor_15_p4, full_adder_com_xor_14_p3
  // halfadder halfadder_5: pin names not known; wires that end beside it: halfadder_4_p3, full_adder_com_xor_15_p4, full_adder_com_xor_14_p2, \Saída5 
endmodule
