// Logisim project Semaforo_Sincronizado.circ as structural Verilog: 4 circuits, main circuit main
module main (
  input  in_1,
  output Et,
  output Et1,
  output Et2
);

  wire and_1_out, and_2_out, and_3_out, and_4_out, and_5_out, circuitoet1_1_out_5, circuitoet2_1_out_5,
       clock_1_out, cores_1_out_3, cores_1_out_4, cores_1_out_5, cores_2_out_3, cores_2_out_4, cores_2_out_5,
       cores_3_out_3, cores_3_out_4, cores_3_out_5, Entrada_out, s_r_ff_1_q;

  S_R_Flip_Flop #(.trigger("high")) s_r_ff_1 (
    .S(Entrada_out), .R(Et), .clk(in_1), .Q(s_r_ff_1_q));  // open: reset, Qn, preset
  Button Entrada (.out(Entrada_out));
  and and_1 (and_1_out, ~Et, Et2, s_r_ff_1_q);  // AND_Gate
  CircuitoEt1 circuitoet1_1 (.in_1(Et), .in_2(s_r_ff_1_q), .in_3(Et1), .in_4(Et2), .out_5(circuitoet1_1_out_5));
  CircuitoEt2 circuitoet2_1 (.in_1(s_r_ff_1_q), .in_2(Et1), .in_3(Et), .in_4(Et2), .out_5(circuitoet2_1_out_5));
  Clock clock_1 (.out(clock_1_out));
  D_Flip_Flop d_ff_1 (.D(and_1_out), .clk(clock_1_out), .Q(Et));  // open: Qn, preset, reset
  D_Flip_Flop d_ff_2 (.D(circuitoet1_1_out_5), .clk(clock_1_out), .Q(Et1));  // open: Qn, preset, reset
  D_Flip_Flop d_ff_3 (.D(circuitoet2_1_out_5), .clk(clock_1_out), .Q(Et2));  // open: Qn, preset, reset
  and and_2 (and_2_out, Et1, ~Et2);  // AND_Gate
  and and_3 (and_3_out, Et1, Et2);
  and and_4 (and_4_out, ~Et, ~Et1, ~Et2);  // AND_Gate
  and and_5 (and_5_out, ~Et, ~Et1, Et2);  // AND_Gate
  cores cores_1 (
    .in_1(and_2_out), .in_2(and_3_out), .out_3(cores_1_out_3), .out_4(cores_1_out_4), .out_5(cores_1_out_5));
  cores cores_2 (
    .in_1(and_2_out), .in_2(and_3_out), .out_3(cores_2_out_3), .out_4(cores_2_out_4), .out_5(cores_2_out_5));
  cores cores_3 (
    .in_1(and_4_out), .in_2(and_5_out), .out_3(cores_3_out_3), .out_4(cores_3_out_4), .out_5(cores_3_out_5));
  LED led_1 (.in(Et));
  LED led_2 (.in(Et));
  LED led_3 (.in(cores_1_out_5));
  LED led_4 (.in(cores_1_out_3));
  LED led_5 (.in(cores_1_out_4));
  LED led_6 (.in(cores_2_out_5));
  LED led_7 (.in(cores_2_out_3));
  LED led_8 (.in(cores_2_out_4));
  LED led_9 (.in(cores_3_out_5));
  LED led_10 (.in(cores_3_out_3));
  LED led_11 (.in(cores_3_out_4));

  // Notes on the sheet:
  //   Semáforo 1
  //   Semáforo 3
  //   Semáforo 2
  //   Semáforo 4
  //   Semáforo 5
endmodule

module cores (
  input  in_1,
  input  in_2,
  output out_3,
  output out_4,
  output out_5
);

  and and_1 (out_3, ~in_1, in_2);  // AND_Gate
  and and_2 (out_4, ~in_2, in_1);  // AND_Gate
  and and_3 (out_5, ~in_1, ~in_2);  // AND_Gate
endmodule

module CircuitoEt1 (
  input  in_1,
  input  in_2,
  input  in_3,
  input  in_4,
  output out_5
);

  wire and_1_out, and_2_out, and_3_out;

  and and_1 (and_1_out, ~in_1, ~in_2, ~in_3, in_4);  // AND_Gate
  and and_2 (and_2_out, in_1, ~in_4);  // AND_Gate
  and and_3 (and_3_out, in_3, ~in_4);  // AND_Gate
  or or_1 (out_5, and_1_out, and_2_out, and_3_out);
endmodule

module CircuitoEt2 (
  input  in_1,
  input  in_2,
  input  in_3,
  input  in_4,
  output out_5
);

  wire and_1_out, and_2_out;

  and and_1 (and_1_out, in_1, in_2);
  and and_2 (and_2_out, ~in_3, ~in_4);  // AND_Gate
  or or_1 (out_5, and_1_out, and_2_out);
endmodule
